# Fritzing sketch twitometer (saved by Fritzing 0.9.4)
breadboards: 2

parts:
  Part1 = Arduino Pro Mini v13
  Raspberry_Pi_1 = Raspberry Pi 3 [part_number=RPI-3-V1.2]  # not connected
  Part3 = Arduino Pro Mini v13
  Part4 = HT SSOP28 pad [chip_label=AX1201728SG package=SSOP]
  Part5 = Adafruit T-Cobbler Plus [part_number="Adafruit #1989 and #2028"]
  8x8_LED_Modul_mit_MAX1 = 8x8 LED Modul mit MAX7219 [package=THT]
  8x8_LED_Modul_mit_MAX2 = 8x8 LED Modul mit MAX7219 [package=THT]  # not connected
  8x8_LED_Modul_mit_MAX3 = 8x8 LED Modul mit MAX7219 [package=THT]  # not connected
  8x8_LED_Modul_mit_MAX4 = 8x8 LED Modul mit MAX7219 [package=THT]
  8x8_LED_Modul_mit_MAX5 = 8x8 LED Modul mit MAX7219 [package=THT]
  8x8_LED_Modul_mit_MAX6 = 8x8 LED Modul mit MAX7219 [package=THT]  # not connected
  8x8_LED_Modul_mit_MAX7 = 8x8 LED Modul mit MAX7219 [package=THT]  # not connected
  8x8_LED_Modul_mit_MAX8 = 8x8 LED Modul mit MAX7219 [package=THT]  # not connected
  M1 = Stepper Motor - Automotive Gauge
  M2 = Stepper Motor - Automotive Gauge
  U1 = DC-DC_CONVERTER [package=dc-dc_converter]
  J1 = Power Jack [package=power_jack_combo]  # not connected
  R1 = Resistor [tolerance=±5% resistance=1.3k package=THT]
  LED2 = LED - 3mm [color="Blue (525nm)" package="3 mm [THT]"]
  LED1 = LED - 3mm [color="Red (633nm)" package="3 mm [THT]"]
  R2 = Resistor [tolerance=±5% resistance=100 package=THT]
  R3 = Resistor [tolerance=±5% resistance=150 package=THT]

nets:
  N1: Part1.A4, Part3.A4, Part5.SDA
  N2: Part1.A5, Part3.A5, Part5.SCL
  GND: Part1.RAW, Part1.GND, Part3.GND, Part3.RAW, Part4.GND, Part4.12, Part4.15, Part5.GND, 8x8_LED_Modul_mit_MAX1.VCC_Eingang, U1.GND1, U1.VOUT, U1.GND2, R1.Pin_1, LED2.cathode, LED1.cathode, R2.Pin_1
  N3: Part1.D13/SCK, 8x8_LED_Modul_mit_MAX1.CLK_Eingang
  N4: Part1.D11_PWM/MOSI, 8x8_LED_Modul_mit_MAX1.GND_Eingang, 8x8_LED_Modul_mit_MAX1.DIN_Eingang
  N5: Part1.D10_PWM/SS, 8x8_LED_Modul_mit_MAX1.CS_Eingang
  N6: Part3.D13/SCK, Part4.27
  N7: Part3.D12/MISO, Part4.26
  N8: Part3.D8, Part4.28
  N9: Part3.D7, Part4.2
  N10: Part3.D4, Part4.3
  N11: Part4.4, M2.pin_1
  N12: Part4.5, M2.pin_2
  N13: Part4.6, M2.pin_3
  N14: Part4.7, M2.pin_4
  N15: Part4.22, M1.pin_4
  N16: Part4.23, M1.pin_3
  N17: Part4.24, M1.pin_2
  N18: Part4.25, M1.pin_1
  N19: Part5.GPIO27, U1.ON_OFF
  N20: 8x8_LED_Modul_mit_MAX4.VCC_Ausgang, 8x8_LED_Modul_mit_MAX5.VCC_Eingang
  N21: 8x8_LED_Modul_mit_MAX4.GND_Ausgang, 8x8_LED_Modul_mit_MAX5.GND_Eingang
  N22: 8x8_LED_Modul_mit_MAX4.DOUT_Ausgang, 8x8_LED_Modul_mit_MAX5.DIN_Eingang
  N23: 8x8_LED_Modul_mit_MAX4.CS_Ausgang, 8x8_LED_Modul_mit_MAX5.CS_Eingang
  N24: 8x8_LED_Modul_mit_MAX4.CLK_Ausgang, 8x8_LED_Modul_mit_MAX5.CLK_Eingang
  N25: U1.TRIM, R1.Pin_0
  N26: LED2.anode, R2.Pin_0
  N27: LED1.anode, R3.Pin_0

custom parts:
  Adafruit T-Cobbler Plus: The Raspberry Pi has landed on the Maker World like a 40-GPIO pinned, quad-USB ported, credit card sized bomb of DIY joy. And while you can use most of our great Model B accessories by hooking up our downgrade cable, its probably a good time to upgrade your set up and accessorize using all of the 40 pins. That's why we now carry the Assembled Adafruit Pi T-Cobbler Plus - Breakout + Cable for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
  Stepper Motor - Automotive Gauge: Simple, Automotive Gauge stepper motor
